# Fritzing sketch H_Bridge_Redux (saved by Fritzing 0.8.5b)
breadboards: 1

parts:
  IC1 = H-Bridge [package=THT]
  M1 = DC Motor
  Arduino1 = Arduino Uno (Rev3)

nets:
  N1: IC1.1Y, M1.pin_2
  GND: IC1.GND2, Arduino1.GND
  N2: IC1.2Y, M1.pin_1
  N3: IC1.VCC2, Arduino1.VIN
  5V: IC1.VCC1

notes:
  Fun with Arduino by Rob Purser is licensed under a
  Creative Commons
  Attribution-NonCommercial-ShareAlike 3.0 Unported License.
  Based on a work at https://sites.google.com/site/funarduino/
  Copyright 2013, Rob Purser
